// Logisim project abcd.circ as structural Verilog: 1 circuit, main circuit main
module main (
  input  D,
  output Q,
  output Q_prime
);

  wire nand_1_out, nand_2_out, not_1_out, undriven, undriven_2;

  not not_1 (not_1_out, undriven);
  nand nand_1 (nand_1_out, undriven, undriven_2);
  nand nand_2 (nand_2_out, undriven_2, not_1_out);
  nor nor_1 (Q, nand_1_out, nand_1_out, Q_prime);
  nor nor_2 (Q_prime, Q, nand_2_out, nand_2_out);

  // Notes on the sheet:
  //   clock
  //   circuit diagram for D flip flop
endmodule
